// Logisim project singleCycleCPU.circ as structural Verilog: 8 circuits, main circuit main
module main (
  input  Reset,
  output [31:0] out_2,
  output out_3,
  output [4:0] out_4,
  output [31:0] out_5,
  output out_6,
  output [4:0] out_7,
  output [31:0] out_8
);

  wire ALUSrc, clk, COMPresult;
  wire [1:0] EXTop, NPCop, RegDst;
  wire [2:0] ALUop, COMPop, DatatoReg;
  wire [31:0] ALUresult, bit_extender_1_out, ext_1_out, grf_1_rd1, MemReadData, multiplexer_3_out,
       npc_1_pcnext, PC_4, PC_q;

  Multiplexer #(.select(2), .width(5)) multiplexer_1 (
    .in0(out_2[15:11]), .in1(out_2[20:16]), .in2({5{1'b1}}), .in3({5{1'b0}}), .out(out_4), .sel(RegDst));  // open: en
  assign bit_extender_1_out = {{31{1'b0}}, COMPresult};  // Bit_Extender bit_extender_1
  NPC npc_1 (
    .PC(PC_q), .imm_26(out_2[25:0]), .Reg(grf_1_rd1), .imm_16(out_2[15:0]), .compare(COMPresult),
    .PCnext(npc_1_pcnext), .NPCop(NPCop));
  Register #(.width(32)) PC (.D(npc_1_pcnext), .Q(PC_q), .clk(clk), .clr(Reset));  // open: en
  Clock clock_1 (.out(clk));
  Multiplexer #(.select(3), .width(32)) multiplexer_2 (
    .in0({ALUresult[31:7], out_7, ALUresult[1:0]}), .in1(MemReadData), .in2(PC_4), .in3(bit_extender_1_out),
    .out(out_5), .sel(DatatoReg));  // open: in4, in5, in6, in7, en
  EXT ext_1 (.imm(out_2[15:0]), .out(ext_1_out), .EXTop(EXTop));
  Adder #(.width(32)) adder_1 (.a(PC_q), .b(32'h4), .out(PC_4));  // open: cin, cout
  GRF grf_1 (
    .A1(out_2[25:21]), .A2(out_2[20:16]), .A3(out_4), .WD(out_5), .RD1(grf_1_rd1), .RD2(out_8), .Clk(clk),
    .Reset(Reset), .WE(out_3));
  ROM #(.addrWidth(5), .dataWidth(32)) rom_1 (.addr(PC_q[6:2]), .data(out_2));  // open: sel
  Multiplexer #(.width(32)) multiplexer_3 (
    .in0(out_8), .in1(ext_1_out), .out(multiplexer_3_out), .sel(ALUSrc));  // open: en
  Controller controller_1 (
    .op(out_2[31:26]), .func(out_2[5:0]), .RegWrite(out_3), .RegDst(RegDst), .EXTop(EXTop), .NPCop(NPCop),
    .ALUSrc(ALUSrc), .ALUop(ALUop), .COMPop(COMPop), .MemWrite(out_6), .DatatoReg(DatatoReg));
  ALU alu_1 (
    .OperatorA(grf_1_rd1), .shanmtC(out_2[10:6]), .OperatorB(multiplexer_3_out),
    .Result({ALUresult[31:7], out_7, ALUresult[1:0]}), .ALUop(ALUop), .COMPop(COMPop), .COMPresult(COMPresult));
  DM dm_1 (
    .MemAddr(out_7), .MemWriteData(out_8), .MemReadData(MemReadData), .MemWrite(out_6), .Reset(Reset),
    .clk(clk));

  // Other names for the same wires on the sheet: ALUresult[6:2] = out_7; MemAddr[4:0] = out_7; Instr[31:0] = out_2;
  //   instr_func[5:0] = out_2[5:0]; instr_imm16[15:0] = out_2[15:0]; instr_imm26[25:0] = out_2[25:0];
  //   instr_shamt[4:0] = out_2[10:6]; instr_rd[4:0] = out_2[15:11]; instr_rt[4:0] = out_2[20:16];
  //   instr_rs[4:0] = out_2[25:21]; instr_op[5:0] = out_2[31:26]; MemData[31:0] = out_8; MemWrite = out_6;
  //   RegAddr[4:0] = out_4; RegData[31:0] = out_5; RegWrite = out_3

  // Notes on the sheet:
  //   contents of rom_1 (hex, n*v repeats v):
  //   20100032 20080001 110482a 11200004 c00000a 2298820 21080001 8000002 ac110000 800000c 94840 3e00008
endmodule

module GRF (
  input  Clk,
  input  Reset,
  input  WE,
  input  [4:0] A1,
  input  [4:0] A2,
  input  [4:0] A3,
  input  [31:0] WD,
  output [31:0] RD1,
  output [31:0] RD2
);

  wire [31:0] demultiplexer_1_out0, demultiplexer_1_out1, demultiplexer_1_out2, demultiplexer_1_out3,
       demultiplexer_1_out4, demultiplexer_1_out5, demultiplexer_1_out6, demultiplexer_1_out7,
       demultiplexer_2_out1, demultiplexer_2_out2, demultiplexer_2_out3, demultiplexer_3_out0,
       demultiplexer_3_out1, demultiplexer_3_out2, demultiplexer_3_out3, demultiplexer_4_out0,
       demultiplexer_4_out1, demultiplexer_4_out2, demultiplexer_4_out3, demultiplexer_5_out0,
       demultiplexer_5_out1, demultiplexer_5_out2, demultiplexer_5_out3, demultiplexer_6_out0,
       demultiplexer_6_out1, demultiplexer_6_out2, demultiplexer_6_out3, demultiplexer_7_out0,
       demultiplexer_7_out1, demultiplexer_7_out2, demultiplexer_7_out3, demultiplexer_8_out0,
       demultiplexer_8_out1, demultiplexer_8_out2, demultiplexer_8_out3, demultiplexer_9_out0,
       demultiplexer_9_out1, demultiplexer_9_out2, demultiplexer_9_out3, multiplexer_1_out,
       multiplexer_2_out, multiplexer_3_out, multiplexer_4_out, multiplexer_5_out, multiplexer_6_out,
       multiplexer_7_out, multiplexer_8_out, multiplexer_10_out, multiplexer_11_out, multiplexer_12_out,
       multiplexer_13_out, multiplexer_14_out, multiplexer_15_out, multiplexer_16_out, multiplexer_17_out,
       register_1_q, register_2_q, register_3_q, register_4_q, register_5_q, register_6_q, register_7_q,
       register_8_q, register_9_q, register_10_q, register_11_q, register_12_q, register_13_q, register_14_q,
       register_15_q, register_16_q, register_17_q, register_18_q, register_19_q, register_20_q,
       register_21_q, register_22_q, register_23_q, register_24_q, register_25_q, register_26_q,
       register_27_q, register_28_q, register_29_q, register_30_q, register_31_q, register_32_q;

  Demultiplexer #(.select(3), .width(32), .tristate("true")) demultiplexer_1 (
    .out0(demultiplexer_1_out0), .out1(demultiplexer_1_out1), .out2(demultiplexer_1_out2),
    .out3(demultiplexer_1_out3), .out4(demultiplexer_1_out4), .out5(demultiplexer_1_out5),
    .out6(demultiplexer_1_out6), .out7(demultiplexer_1_out7), .in(WD), .sel(A3[2:0]));  // open: en
  Demultiplexer #(.select(2), .width(32), .tristate("true")) demultiplexer_2 (
    .out1(demultiplexer_2_out1), .out2(demultiplexer_2_out2), .out3(demultiplexer_2_out3),
    .in(demultiplexer_1_out0), .sel(A3[4:3]));  // open: out0, en
  Demultiplexer #(.select(2), .width(32), .tristate("true")) demultiplexer_3 (
    .out0(demultiplexer_3_out0), .out1(demultiplexer_3_out1), .out2(demultiplexer_3_out2),
    .out3(demultiplexer_3_out3), .in(demultiplexer_1_out1), .sel(A3[4:3]));  // open: en
  Demultiplexer #(.select(2), .width(32), .tristate("true")) demultiplexer_4 (
    .out0(demultiplexer_4_out0), .out1(demultiplexer_4_out1), .out2(demultiplexer_4_out2),
    .out3(demultiplexer_4_out3), .in(demultiplexer_1_out2), .sel(A3[4:3]));  // open: en
  Demultiplexer #(.select(2), .width(32), .tristate("true")) demultiplexer_5 (
    .out0(demultiplexer_5_out0), .out1(demultiplexer_5_out1), .out2(demultiplexer_5_out2),
    .out3(demultiplexer_5_out3), .in(demultiplexer_1_out3), .sel(A3[4:3]));  // open: en
  Demultiplexer #(.select(2), .width(32), .tristate("true")) demultiplexer_6 (
    .out0(demultiplexer_6_out0), .out1(demultiplexer_6_out1), .out2(demultiplexer_6_out2),
    .out3(demultiplexer_6_out3), .in(demultiplexer_1_out4), .sel(A3[4:3]));  // open: en
  Demultiplexer #(.select(2), .width(32), .tristate("true")) demultiplexer_7 (
    .out0(demultiplexer_7_out0), .out1(demultiplexer_7_out1), .out2(demultiplexer_7_out2),
    .out3(demultiplexer_7_out3), .in(demultiplexer_1_out5), .sel(A3[4:3]));  // open: en
  Demultiplexer #(.select(2), .width(32), .tristate("true")) demultiplexer_8 (
    .out0(demultiplexer_8_out0), .out1(demultiplexer_8_out1), .out2(demultiplexer_8_out2),
    .out3(demultiplexer_8_out3), .in(demultiplexer_1_out6), .sel(A3[4:3]));  // open: en
  Demultiplexer #(.select(2), .width(32), .tristate("true")) demultiplexer_9 (
    .out0(demultiplexer_9_out0), .out1(demultiplexer_9_out1), .out2(demultiplexer_9_out2),
    .out3(demultiplexer_9_out3), .in(demultiplexer_1_out7), .sel(A3[4:3]));  // open: en
  Register #(.width(32)) register_1 (.en(WE), .Q(register_1_q), .clk(Clk), .clr(Reset));  // open: D
  Register #(.width(32)) register_2 (.D(demultiplexer_3_out0), .en(WE), .Q(register_2_q), .clk(Clk), .clr(Reset));
  Register #(.width(32)) register_3 (.D(demultiplexer_4_out0), .en(WE), .Q(register_3_q), .clk(Clk), .clr(Reset));
  Register #(.width(32)) register_4 (.D(demultiplexer_5_out0), .en(WE), .Q(register_4_q), .clk(Clk), .clr(Reset));
  Register #(.width(32)) register_5 (.D(demultiplexer_6_out0), .en(WE), .Q(register_5_q), .clk(Clk), .clr(Reset));
  Register #(.width(32)) register_6 (.D(demultiplexer_7_out0), .en(WE), .Q(register_6_q), .clk(Clk), .clr(Reset));
  Register #(.width(32)) register_7 (.D(demultiplexer_8_out0), .en(WE), .Q(register_7_q), .clk(Clk), .clr(Reset));
  Register #(.width(32)) register_8 (.D(demultiplexer_9_out0), .en(WE), .Q(register_8_q), .clk(Clk), .clr(Reset));
  Register #(.width(32)) register_9 (.D(demultiplexer_2_out1), .en(WE), .Q(register_9_q), .clk(Clk), .clr(Reset));
  Register #(.width(32)) register_10 (.D(demultiplexer_3_out1), .en(WE), .Q(register_10_q), .clk(Clk), .clr(Reset));
  Register #(.width(32)) register_11 (.D(demultiplexer_4_out1), .en(WE), .Q(register_11_q), .clk(Clk), .clr(Reset));
  Register #(.width(32)) register_12 (.D(demultiplexer_5_out1), .en(WE), .Q(register_12_q), .clk(Clk), .clr(Reset));
  Register #(.width(32)) register_13 (.D(demultiplexer_6_out1), .en(WE), .Q(register_13_q), .clk(Clk), .clr(Reset));
  Register #(.width(32)) register_14 (.D(demultiplexer_7_out1), .en(WE), .Q(register_14_q), .clk(Clk), .clr(Reset));
  Register #(.width(32)) register_15 (.D(demultiplexer_8_out1), .en(WE), .Q(register_15_q), .clk(Clk), .clr(Reset));
  Register #(.width(32)) register_16 (.D(demultiplexer_9_out1), .en(WE), .Q(register_16_q), .clk(Clk), .clr(Reset));
  Register #(.width(32)) register_17 (.D(demultiplexer_2_out2), .en(WE), .Q(register_17_q), .clk(Clk), .clr(Reset));
  Register #(.width(32)) register_18 (.D(demultiplexer_3_out2), .en(WE), .Q(register_18_q), .clk(Clk), .clr(Reset));
  Register #(.width(32)) register_19 (.D(demultiplexer_4_out2), .en(WE), .Q(register_19_q), .clk(Clk), .clr(Reset));
  Register #(.width(32)) register_20 (.D(demultiplexer_5_out2), .en(WE), .Q(register_20_q), .clk(Clk), .clr(Reset));
  Register #(.width(32)) register_21 (.D(demultiplexer_6_out2), .en(WE), .Q(register_21_q), .clk(Clk), .clr(Reset));
  Register #(.width(32)) register_22 (.D(demultiplexer_7_out2), .en(WE), .Q(register_22_q), .clk(Clk), .clr(Reset));
  Register #(.width(32)) register_23 (.D(demultiplexer_8_out2), .en(WE), .Q(register_23_q), .clk(Clk), .clr(Reset));
  Register #(.width(32)) register_24 (.D(demultiplexer_9_out2), .en(WE), .Q(register_24_q), .clk(Clk), .clr(Reset));
  Register #(.width(32)) register_25 (.D(demultiplexer_2_out3), .en(WE), .Q(register_25_q), .clk(Clk), .clr(Reset));
  Register #(.width(32)) register_26 (.D(demultiplexer_3_out3), .en(WE), .Q(register_26_q), .clk(Clk), .clr(Reset));
  Register #(.width(32)) register_27 (.D(demultiplexer_4_out3), .en(WE), .Q(register_27_q), .clk(Clk), .clr(Reset));
  Register #(.width(32)) register_28 (.D(demultiplexer_5_out3), .en(WE), .Q(register_28_q), .clk(Clk), .clr(Reset));
  Register #(.width(32)) register_29 (.D(demultiplexer_6_out3), .en(WE), .Q(register_29_q), .clk(Clk), .clr(Reset));
  Register #(.width(32)) register_30 (.D(demultiplexer_7_out3), .en(WE), .Q(register_30_q), .clk(Clk), .clr(Reset));
  Register #(.width(32)) register_31 (.D(demultiplexer_8_out3), .en(WE), .Q(register_31_q), .clk(Clk), .clr(Reset));
  Register #(.width(32)) register_32 (.D(demultiplexer_9_out3), .en(WE), .Q(register_32_q), .clk(Clk), .clr(Reset));
  Multiplexer #(.select(2), .width(32)) multiplexer_1 (
    .in0(register_1_q), .in1(register_9_q), .in2(register_17_q), .in3(register_25_q),
    .out(multiplexer_1_out), .sel(A1[4:3]));  // open: en
  Multiplexer #(.select(2), .width(32)) multiplexer_2 (
    .in0(register_2_q), .in1(register_10_q), .in2(register_18_q), .in3(register_26_q),
    .out(multiplexer_2_out), .sel(A1[4:3]));  // open: en
  Multiplexer #(.select(2), .width(32)) multiplexer_3 (
    .in0(register_3_q), .in1(register_11_q), .in2(register_19_q), .in3(register_27_q),
    .out(multiplexer_3_out), .sel(A1[4:3]));  // open: en
  Multiplexer #(.select(2), .width(32)) multiplexer_4 (
    .in0(register_4_q), .in1(register_12_q), .in2(register_20_q), .in3(register_28_q),
    .out(multiplexer_4_out), .sel(A1[4:3]));  // open: en
  Multiplexer #(.select(2), .width(32)) multiplexer_5 (
    .in0(register_5_q), .in1(register_13_q), .in2(register_21_q), .in3(register_29_q),
    .out(multiplexer_5_out), .sel(A1[4:3]));  // open: en
  Multiplexer #(.select(2), .width(32)) multiplexer_6 (
    .in0(register_6_q), .in1(register_14_q), .in2(register_22_q), .in3(register_30_q),
    .out(multiplexer_6_out), .sel(A1[4:3]));  // open: en
  Multiplexer #(.select(2), .width(32)) multiplexer_7 (
    .in0(register_7_q), .in1(register_15_q), .in2(register_23_q), .in3(register_31_q),
    .out(multiplexer_7_out), .sel(A1[4:3]));  // open: en
  Multiplexer #(.select(2), .width(32)) multiplexer_8 (
    .in0(register_8_q), .in1(register_16_q), .in2(register_24_q), .in3(register_32_q),
    .out(multiplexer_8_out), .sel(A1[4:3]));  // open: en
  Multiplexer #(.select(3), .width(32)) multiplexer_9 (
    .in0(multiplexer_1_out), .in1(multiplexer_2_out), .in2(multiplexer_3_out), .in3(multiplexer_4_out),
    .in4(multiplexer_5_out), .in5(multiplexer_6_out), .in6(multiplexer_7_out), .in7(multiplexer_8_out),
    .out(RD1), .sel(A1[2:0]));  // open: en
  Multiplexer #(.select(2), .width(32)) multiplexer_10 (
    .in0(register_3_q), .in1(register_11_q), .in2(register_19_q), .in3(register_27_q),
    .out(multiplexer_10_out), .sel(A2[4:3]));  // open: en
  Multiplexer #(.select(2), .width(32)) multiplexer_11 (
    .in0(register_4_q), .in1(register_12_q), .in2(register_20_q), .in3(register_28_q),
    .out(multiplexer_11_out), .sel(A2[4:3]));  // open: en
  Multiplexer #(.select(2), .width(32)) multiplexer_12 (
    .in0(register_5_q), .in1(register_13_q), .in2(register_21_q), .in3(register_29_q),
    .out(multiplexer_12_out), .sel(A2[4:3]));  // open: en
  Multiplexer #(.select(2), .width(32)) multiplexer_13 (
    .in0(register_6_q), .in1(register_14_q), .in2(register_22_q), .in3(register_30_q),
    .out(multiplexer_13_out), .sel(A2[4:3]));  // open: en
  Multiplexer #(.select(2), .width(32)) multiplexer_14 (
    .in0(register_7_q), .in1(register_15_q), .in2(register_23_q), .in3(register_31_q),
    .out(multiplexer_14_out), .sel(A2[4:3]));  // open: en
  Multiplexer #(.select(2), .width(32)) multiplexer_15 (
    .in0(register_8_q), .in1(register_16_q), .in2(register_24_q), .in3(register_32_q),
    .out(multiplexer_15_out), .sel(A2[4:3]));  // open: en
  Multiplexer #(.select(2), .width(32)) multiplexer_16 (
    .in0(register_1_q), .in1(register_9_q), .in2(register_17_q), .in3(register_25_q),
    .out(multiplexer_16_out), .sel(A2[4:3]));  // open: en
  Multiplexer #(.select(2), .width(32)) multiplexer_17 (
    .in0(register_2_q), .in1(register_10_q), .in2(register_18_q), .in3(register_26_q),
    .out(multiplexer_17_out), .sel(A2[4:3]));  // open: en
  Multiplexer #(.select(3), .width(32)) multiplexer_18 (
    .in0(multiplexer_16_out), .in1(multiplexer_17_out), .in2(multiplexer_10_out), .in3(multiplexer_11_out),
    .in4(multiplexer_12_out), .in5(multiplexer_13_out), .in6(multiplexer_14_out), .in7(multiplexer_15_out),
    .out(RD2), .sel(A2[2:0]));  // open: en

  // Other names for the same wires on the sheet: A1_low[2:0] = A1[2:0]; A1_high[1:0] = A1[4:3]; A2_low[2:0] = A2[2:0];
  //   A2_high[1:0] = A2[4:3]; A3_low[2:0] = A3[2:0]; A3_high[1:0] = A3[4:3]

  // Notes on the sheet:
  //   0
  //   8
  //   16
  //   24
endmodule

module ALU (
  input  [2:0] ALUop,
  input  [31:0] OperatorA,
  input  [4:0] shanmtC,
  input  [2:0] COMPop,
  input  [31:0] OperatorB,
  output [31:0] Result,
  output COMPresult
);

  wire [31:0] A___B, A___B_t, B___C, B__C, B__C_t, sub, sum;

  assign A___B = OperatorB & OperatorA;  // AND_Gate and_1, 32 bits wide
  Shifter #(.width(32), .shift("ar")) shifter_1 (.in(OperatorB), .\dist (shanmtC), .out(B___C));
  Adder #(.width(32)) adder_1 (.a(OperatorB), .b(OperatorA), .out(sum));  // open: cin, cout
  Subtractor #(.width(32)) subtractor_1 (.a(OperatorA), .b(OperatorB), .out(sub));  // open: bin, bout
  assign A___B_t = OperatorA | OperatorB;  // OR_Gate or_1, 32 bits wide
  Shifter #(.width(32), .shift("lr")) shifter_2 (.in(OperatorB), .\dist (shanmtC), .out(B__C_t));
  Shifter #(.width(32)) shifter_3 (.in(OperatorB), .\dist (shanmtC), .out(B__C));
  Multiplexer #(.select(3), .width(32)) multiplexer_1 (
    .in0(sum), .in1(sub), .in2(A___B_t), .in3(A___B), .in4(B__C_t), .in5(B__C), .in6(B___C), .out(Result),
    .sel(ALUop));  // open: in7, en
  COMP comp_1 (.operationA(OperatorA), .operationB(OperatorB), .COMPresult(COMPresult), .COMPop(COMPop));

  // Other names for the same wires on the sheet: Sel[2:0] = ALUop

  // Notes on the sheet:
  //   opB
  //   shamtC
  //   opB
  //   opA
  //   opA
  //   opB
  //   opB
  //   shamtC
  //   opB
  //   shamtC
  //   opA
  //   opA
  //   opB
  //   opB
  //   opA
  //   opA
  //   opB
  //   opB
  //   000 : A+B
  //   001 : A - B
endmodule

module COMP (
  input  [2:0] COMPop,
  input  [31:0] operationA,
  input  [31:0] operationB,
  output COMPresult
);

  wire comparator_1_eq, comparator_1_gt, comparator_1_lt, comparator_2_gt, comparator_2_lt, not_1_out;

  Comparator #(.width(32)) comparator_1 (
    .a(operationA), .b(operationB), .gt(comparator_1_gt), .eq(comparator_1_eq), .lt(comparator_1_lt));
  Comparator #(.width(32), .mode("unsigned")) comparator_2 (
    .a(operationA), .b(operationB), .gt(comparator_2_gt), .lt(comparator_2_lt));  // open: eq
  not not_1 (not_1_out, comparator_1_eq);
  Multiplexer #(.select(3)) multiplexer_1 (
    .in0(comparator_1_eq), .in1(comparator_1_lt), .in2(comparator_1_gt), .in3(comparator_2_lt),
    .in4(comparator_2_gt), .in5(not_1_out), .in6(1'b0), .in7(1'b0), .out(COMPresult), .sel(COMPop));  // open: en

  // Other names for the same wires on the sheet: sel[2:0] = COMPop

  // Notes on the sheet:
  //   000:A==B
  //   001:A<B有符号
  //   010:A>B有符号
  //   011:A<B无符号
  //   100:A>B无符号
  //   101:A!=B
endmodule

module NPC (
  input  [1:0] NPCop,
  input  [31:0] PC,
  input  [25:0] imm_26,
  input  [31:0] Reg,
  input  [15:0] imm_16,
  input  compare,
  output [31:0] PCnext
);

  wire [31:0] adder_2_out, bit_extender_1_out, \I型 , PC_4;

  assign bit_extender_1_out = {{14{imm_16[15]}}, {imm_16, 2'b00}};  // Bit_Extender bit_extender_1
  Adder #(.width(32)) adder_1 (.a(PC), .b(32'h4), .out(PC_4));  // open: cin, cout
  Adder #(.width(32)) adder_2 (.a(PC_4), .b(bit_extender_1_out), .out(adder_2_out));  // open: cin, cout
  Multiplexer #(.width(32)) multiplexer_1 (.in0(PC_4), .in1(adder_2_out), .out(\I型 ), .sel(compare));  // open: en
  Multiplexer #(.select(2), .width(32)) multiplexer_2 (
    .in0(PC_4), .in1(\I型 ), .in2({PC[31:28], imm_26, 2'b00}), .in3(Reg), .out(PCnext), .sel(NPCop));  // open: en

  // Other names for the same wires on the sheet: J型[31:2] = {PC[31:28], imm_26}; regAddr[31:0] = Reg;
  //   sel[1:0] = NPCop
endmodule

module DM (
  input  [4:0] MemAddr,
  input  [31:0] MemWriteData,
  input  Reset,
  input  MemWrite,
  input  clk,
  output [31:0] MemReadData
);

  RAM #(.addrWidth(5), .dataWidth(32), .bus("separate")) ram_1 (
    .addr(MemAddr), .din(MemWriteData), .data(MemReadData), .str(MemWrite), .clk(clk), .clr(Reset));  // open: sel, ld
endmodule

module EXT (
  input  [1:0] EXTop,
  input  [15:0] imm,
  output [31:0] out
);

  wire [31:0] bit_extender_1_out, bit_extender_2_out, shifter_1_out;

  assign bit_extender_1_out = {{16{imm[15]}}, imm};  // Bit_Extender bit_extender_1
  assign bit_extender_2_out = {{16{1'b0}}, imm};  // Bit_Extender bit_extender_2
  Shifter #(.width(32)) shifter_1 (.in(bit_extender_2_out), .\dist (5'b10000), .out(shifter_1_out));
  Multiplexer #(.select(2), .width(32)) multiplexer_1 (
    .in0(bit_extender_1_out), .in1(bit_extender_2_out), .in2(shifter_1_out), .out(out), .sel(EXTop));  // open: in3, en

  // Other names for the same wires on the sheet: sel[1:0] = EXTop

  // Notes on the sheet:
  //   00:符号扩展；01：无符号扩展；10：立即数逻辑左移16位
endmodule

module Controller (
  input  [5:0] op,
  input  [5:0] func,
  output RegWrite,
  output MemWrite,
  output [1:0] NPCop,
  output [2:0] ALUop,
  output [2:0] COMPop,
  output [1:0] RegDst,
  output ALUSrc,
  output [1:0] EXTop,
  output [2:0] DatatoReg
);

  wire add, addi, beq, bne, J, jal, jr, lui, lw, not_1_out, not_2_out, not_3_out, not_4_out, not_5_out,
       not_6_out, not_7_out, not_8_out, not_9_out, not_10_out, not_11_out, not_12_out, Ori, \R型指令_out , sll,
       slt, sub, sw;

  not not_1 (not_1_out, op[5]);
  not not_2 (not_2_out, op[4]);
  not not_3 (not_3_out, func[4]);
  not not_4 (not_4_out, func[5]);
  not not_5 (not_5_out, op[2]);
  not not_6 (not_6_out, op[3]);
  not not_7 (not_7_out, func[2]);
  not not_8 (not_8_out, func[3]);
  not not_9 (not_9_out, op[0]);
  not not_10 (not_10_out, op[1]);
  not not_11 (not_11_out, func[0]);
  not not_12 (not_12_out, func[1]);
  and \R型指令  (\R型指令_out , not_9_out, not_10_out, not_5_out, not_6_out, not_2_out, not_1_out);
  and u_ori (Ori, op[0], not_10_out, op[2], op[3], not_2_out, not_1_out);
  and u_sw (sw, op[0], op[1], not_5_out, op[3], not_2_out, op[5]);
  and u_lw (lw, op[0], op[1], not_5_out, not_6_out, not_2_out, op[5]);
  and u_lui (lui, op[0], op[1], op[2], op[3], not_2_out, not_1_out);
  and u_beq (beq, not_9_out, not_10_out, op[2], not_6_out, not_2_out, not_1_out);
  and u_J (J, not_9_out, op[1], not_5_out, not_6_out, not_2_out, not_1_out);
  and u_addi (addi, not_9_out, not_10_out, not_5_out, op[3], not_2_out, not_1_out);
  and u_bne (bne, op[0], not_10_out, op[2], not_6_out, not_2_out, not_1_out);
  and u_add (add, \R型指令_out , not_12_out, not_7_out, not_11_out, not_8_out, not_3_out, func[5]);
  and u_sub (sub, not_11_out, func[1], not_7_out, \R型指令_out , not_8_out, not_3_out, func[5]);
  and u_slt (slt, not_11_out, func[1], not_7_out, \R型指令_out , func[3], not_3_out, func[5]);
  and u_sll (sll, not_11_out, not_12_out, not_7_out, \R型指令_out , not_8_out, not_3_out, not_4_out);
  and u_jal (jal, op[0], op[1], not_5_out, not_6_out, not_2_out, not_1_out);
  and sll_2 (jr, not_11_out, not_12_out, not_7_out, \R型指令_out , func[3], not_3_out, not_4_out);
  or or_1 (RegWrite, add, 1'b0, Ori, lw, sub, lui, addi, slt, sll, jal);
  or or_2 (RegDst[1], 1'b0, jal);
  or or_3 (RegDst[0], 1'b0, addi, lui, Ori, lw);
  or or_4 (EXTop[1], 1'b0, lui);
  or or_5 (EXTop[0], Ori, 1'b0);
  or or_6 (NPCop[1], 1'b0, jal, J, jr);
  or or_7 (NPCop[0], 1'b0, bne, beq, jr);
  or or_8 (ALUSrc, addi, 1'b0, lui, lw, sw, Ori);
  or or_9 (ALUop[2], 1'b0, sll);
  or or_10 (ALUop[1], 1'b0, Ori);
  or or_11 (ALUop[0], 1'b0, sll, sub);
  or or_12 (COMPop[2], 1'b0, bne);
  buf or_13 (COMPop[1], 1'b0);  // OR_Gate
  or or_14 (COMPop[0], 1'b0, slt, bne);
  or or_15 (MemWrite, 1'b0, sw);
  buf or_16 (DatatoReg[2], 1'b0);  // OR_Gate
  or or_17 (DatatoReg[1], 1'b0, jal, slt);
  or or_18 (DatatoReg[0], 1'b0, lw, slt);

  // Notes on the sheet:
  //   5
  //   4
  //   3
  //   2
  //   1
  //   0
  //   001101
  //   1
  //   0
  //   1
  //   0
  //   1
  //   2
  //   2
  //   0
  //   1
  //   0
  //   2
  //   1
  //   0
endmodule
